# Fritzing sketch rpi-poweroff (saved by Fritzing 0.8.5b)
breadboards: 1

parts:
  Raspberry_Pi_1 = Raspberry Pi 3
  Q1 = TIP120 Hi-Current Darlington Transistor
  U2 = Mini-USB _B_ connector with 5th pin broken out. [package=usb-minib]  # not connected
  Adafruit_Atmega32u1 = Adafruit Atmega32u4 Breakout Board [part_number="Atmega 32u4"]
  R2 = Resistor [tolerance=±10% resistance=4.7k package="0805 [SMD]"]
  R3 = Resistor [tolerance=±10% resistance=330 package="0805 [SMD]"]

nets:
  N1: Raspberry_Pi_1.3v3, R2.Pin_0
  N2: Raspberry_Pi_1.GIPO17, Adafruit_Atmega32u1.D6
  N3: Raspberry_Pi_1.GND, Q1.COLLECTOR, Adafruit_Atmega32u1.D0, Adafruit_Atmega32u1.D4, R2.Pin_1
  5V: Raspberry_Pi_1.5V, Adafruit_Atmega32u1.VCC
  N4: Q1.BASE, R3.Pin_0
  N5: Q1.EMITTER, Adafruit_Atmega32u1.GND
  N6: Adafruit_Atmega32u1.F5, Adafruit_Atmega32u1.B3, Adafruit_Atmega32u1.D2, R3.Pin_1
